// Logisim project cpu_backup.circ as structural Verilog: 7 circuits, main circuit cpu
module cpu (
);

  wire alu_1_equal, and_1_out, and_2_out, \byte , clock_1_out, comparator_1_eq, compare_1_result,
       control_1_branch, \control_1_dm写入使能 , \control_1_hilo写入使能 , control_1_jr, control_1_jump,
       control_1_set, control_1_systemcall, \control_1_寄存器写入使能 , nand_1_out, not_1_out, npc_1_branch_success,
       systemout_q, \继续_out ;
  wire [1:0] alu_1_result, \control_1_alu_src_2位_s_ext_rfd2_s_extun_0 , control_1_op_compare,
       \control_1_寄存器写入数据选择2位_alu_dm_pc_lo ;
  wire [3:0] control_1_alu_op;
  wire [4:0] control_1_ra, control_1_rb, control_1_rw;
  wire [9:0] alu_1_result_2;
  wire [15:0] \总周期数 , \无条件分支指令数 , \有条件分支成功跳转 , \有条件分支指令数 ;
  wire [27:0] control_1_imme;
  wire [31:0] control_1_signed, control_1_unsigned, LO_q, mips_ram_1_p6, multiplexer_1_out,
       multiplexer_2_out, npc_1_pc_4, npc_1_pc_out, PC_q, registerfile_1_p1, registerfile_1_p7,
       registerfile_1_p8, rom_1_data, SyscallOut;
  wire [31:12] alu_1_result_3;

  nand nand_1 (nand_1_out, control_1_systemcall, ~alu_1_equal, not_1_out);  // NAND_Gate
  Button \u_继续  (.out(\继续_out ));
  Clock clock_1 (.out(clock_1_out));
  Register #(.width(32)) PC (.D(npc_1_pc_out), .en(nand_1_out), .Q(PC_q), .clk(clock_1_out));  // open: clr
  not not_1 (not_1_out, \继续_out );
  Hex_Digit_Display hex_digit_display_1 (.value(SyscallOut[31:28]));  // open: dp
  Hex_Digit_Display hex_digit_display_2 (.value(SyscallOut[27:24]));  // open: dp
  Register #(.width(1)) systemout (.D(nand_1_out), .Q(systemout_q), .clk(clock_1_out));  // open: en, clr
  Hex_Digit_Display hex_digit_display_3 (.value(SyscallOut[19:16]));  // open: dp
  Hex_Digit_Display hex_digit_display_4 (.value(SyscallOut[23:20]));  // open: dp
  Counter #(.width(16), .max('hffff)) counter_1 (.Q(\总周期数 ), .clk(and_1_out));  // open: load, D, count, carry, clr
  and and_1 (and_1_out, clock_1_out, systemout_q);
  Hex_Digit_Display hex_digit_display_5 (.value(SyscallOut[11:8]));  // open: dp
  Hex_Digit_Display hex_digit_display_6 (.value(SyscallOut[15:12]));  // open: dp
  Control control_1 (
    .\寄存器写入使能 (\control_1_寄存器写入使能 ),
    .\ALU_SRC_2位_s_ext_RFD2_s_extun_0 (\control_1_alu_src_2位_s_ext_rfd2_s_extun_0 ),
    .\HILO写入使能 (\control_1_hilo写入使能 ), .OP_compare(control_1_op_compare),
    .\寄存器写入数据选择2位_alu_DM_PC_LO (\control_1_寄存器写入数据选择2位_alu_dm_pc_lo ), .JUMP(control_1_jump),
    .ALU_OP(control_1_alu_op), .Byte(\byte ), .JR(control_1_jr), .Systemcall(control_1_systemcall),
    .set(control_1_set), .\DM写入使能 (\control_1_dm写入使能 ), .Branch(control_1_branch), .CMD(rom_1_data),
    .\signed (control_1_signed), .\unsigned (control_1_unsigned), .imme(control_1_imme), .RA(control_1_ra),
    .RW(control_1_rw), .RB(control_1_rb));
  ROM #(.addrWidth(10), .dataWidth(32)) rom_1 (.addr(PC_q[11:2]), .data(rom_1_data));  // open: sel
  Hex_Digit_Display hex_digit_display_7 (.value(SyscallOut[7:4]));  // open: dp
  Hex_Digit_Display hex_digit_display_8 (.value(SyscallOut[3:0]));  // open: dp
  LED \u_有条件跳转成功  (.in(npc_1_branch_success));
  \分支计数  \u_分支计数_1  (
    .J(control_1_jump), .B(control_1_branch), .S(npc_1_branch_success), .T(clock_1_out), .JO(\无条件分支指令数 ),
    .BO(\有条件分支指令数 ), .BS(\有条件分支成功跳转 ));
  NPC npc_1 (
    .branch_success(npc_1_branch_success), ._5or16(control_1_signed), .imme(control_1_imme), .PC(PC_q),
    .BRANCH(control_1_branch), .RFD1(registerfile_1_p7), .JUMP(control_1_jump), .JR(control_1_jr),
    .compare_result(compare_1_result), .PC_out(npc_1_pc_out), .PC_4(npc_1_pc_4));
  // Probe on \总周期数 
  // Probe on \无条件分支指令数 
  // Probe on \有条件分支指令数 
  // Probe on \有条件分支成功跳转 
  Comparator #(.width(5), .mode("unsigned")) comparator_1 (
    .a(control_1_rw), .b(5'b00100), .eq(comparator_1_eq));  // open: gt, lt
  // RegisterFile registerfile_1: pin names not known; wires that end beside it: registerfile_1_p1, clock_1_out, \control_1_寄存器写入使能 , control_1_rw, control_1_ra, control_1_rb, registerfile_1_p7, registerfile_1_p8
  Register #(.width(32)) systemcall (
    .D(registerfile_1_p1), .en(and_2_out), .Q(SyscallOut), .clk(clock_1_out));  // open: clr
  and and_2 (and_2_out, comparator_1_eq, \control_1_寄存器写入使能 );
  Multiplexer #(.select(2), .width(32), .disabled(0)) multiplexer_1 (
    .in0(control_1_signed), .in1(registerfile_1_p8), .in2(control_1_unsigned), .in3({32{1'b0}}),
    .out(multiplexer_1_out), .sel(\control_1_alu_src_2位_s_ext_rfd2_s_extun_0 ));  // open: en
  Multiplexer #(.width(32), .disabled(0)) multiplexer_2 (
    .in0(multiplexer_1_out), .in1(32'h22), .out(multiplexer_2_out), .sel(control_1_systemcall));  // open: en
  ALU alu_1 (
    .AluOP(control_1_alu_op), .X(registerfile_1_p7), .Equal(alu_1_equal),
    .Result({alu_1_result_3, alu_1_result_2, alu_1_result}), .Y(multiplexer_2_out));  // open: Signed_Overflow, Result_2, UnSigned_Overflow
  compare compare_1 (
    .result(compare_1_result), .choice(control_1_op_compare), .\等于 (alu_1_equal), .\小于 (alu_1_result[0]));
  Register #(.width(32)) LO (
    .D({alu_1_result_3, alu_1_result_2, alu_1_result}), .en(\control_1_hilo写入使能 ), .Q(LO_q), .clk(clock_1_out));  // open: clr
  // MIPS_RAM mips_ram_1: pin names not known; wires that end beside it: alu_1_result_2, registerfile_1_p8, \control_1_dm写入使能 , clock_1_out, 1'b1, mips_ram_1_p6
  data_in_re data_in_re_1 (
    .result({alu_1_result_3, alu_1_result_2, alu_1_result}), .data(mips_ram_1_p6), .sel(alu_1_result),
    .PC_4(npc_1_pc_4), .\byte (\byte ), .LO(LO_q), .re_choose(\control_1_寄存器写入数据选择2位_alu_dm_pc_lo ),
    .in_8(alu_1_result[0]), .set(control_1_set), .data_in_re(registerfile_1_p1));

  // Notes on the sheet:
  //   数码管输出应该用寄存器锁存，否则显示数据只能一闪而过
  //   可以通过项目增加Logisim库的方式将前几次实验完成的电路作为子电路引入到本电路中使用
  //   指令存储器
  //   contents of rom_1 (hex, n*v repeats v):
  //   341d0400 341e0400 c000c05 3402000a c afbf0000 afbefffc 3a0f021 34010024 afa1ffe0 3a1e822 8fc8ffe4
  //   34080064 afc8ffe4 8fc9fff4 3409000a afc9fff4 1202821 afc8ffe4 afc9fff4 c000c23 8fc8ffe8 404021
  //   8fc9fff8 1004821 afc9fff8 1202021 34020022 c 8fa10004 3a1e820 8fbf0000 8fbefffc 1021 3e00008
  //   afbf0000 afbefffc 3a0f021 34010034 afa1ffd0 3a1e822 8fc8ffd4 34080000 afc8ffd4 8fc9ffd8 34090000
  //   afc9ffd8 8fcaffe8 1205021 afcaffe8 8fcbffec a05821 afcbffec 14b082a 2021ffff 10200001 8000c50
  //   8fccffdc 1006021 afccffdc 8fcdffe0 1206821 afcdffe0 18d4020 afc8ffd4 8fceffe4 1007021 afceffe4
  //   1c02021 34020022 c 8fcffff0 1207821 afcffff0 8fd0fff4 34100001 afd0fff4 1f04820 afc9ffd8 8000c2f
  //   8fd1fff8 1008821 afd1fff8 8fa10004 3a1e820 8fbf0000 8fbefffc 2201021 3e00008
  //   数码管输出
  //   总复位信号应将除ROM以外所有存储组件全部清零
  //   寄存器文件
endmodule

module Decode (
  input  [31:0] CMD,
  output [31:0] s_ext_16,
  output [27:0] immi_28,
  output [5:0] FUNC,
  output [5:0] OP,
  output [4:0] RS,
  output [31:0] s_ext_5,
  output [4:0] RT,
  output [4:0] RD,
  output [31:0] s_extun_16
);

  wire [31:0] bit_extender_1_out;
  wire [31:28] shifter_1_out;

  assign bit_extender_1_out = {{6{CMD[25]}}, CMD[25:0]};  // Bit_Extender bit_extender_1
  Shifter #(.width(32)) shifter_1 (.in(bit_extender_1_out), .\dist (5'b00010), .out({shifter_1_out, immi_28}));
  assign s_ext_16 = {{16{CMD[15]}}, CMD[15:0]};  // Bit_Extender bit_extender_2
  assign s_extun_16 = {{16{1'b0}}, CMD[15:0]};  // Bit_Extender bit_extender_3
  assign s_ext_5 = {{27{1'b0}}, CMD[10:6]};  // Bit_Extender bit_extender_4

  assign FUNC = CMD[5:0];
  assign OP = CMD[31:26];
  assign RD = CMD[15:11];
  assign RS = CMD[25:21];
  assign RT = CMD[20:16];

  // Other names for the same wires on the sheet: immi[27:0] = immi_28

  // Notes on the sheet:
  //   输入引脚区
  //   输出引脚区
endmodule

module Control (
  input  [31:0] CMD,
  output [31:0] \signed ,
  output [4:0] RA,
  output \HILO写入使能 ,
  output Branch,
  output [4:0] RB,
  output [31:0] \unsigned ,
  output JUMP,
  output [4:0] RW,
  output [27:0] imme,
  output JR,
  output \寄存器写入使能 ,
  output \DM写入使能 ,
  output [1:0] \寄存器写入数据选择2位_alu_DM_PC_LO ,
  output [1:0] OP_compare,
  output Byte,
  output [1:0] \ALU_SRC_2位_s_ext_RFD2_s_extun_0 ,
  output set,
  output [3:0] ALU_OP,
  output Systemcall
);

  wire ADD, ADDI, ADDIU, ADDU, AND, ANDI, BEQ, BLEZ, BNE, demultiplexer_1_out0, demultiplexer_1_out1,
       demultiplexer_1_out2, demultiplexer_1_out3, demultiplexer_1_out4, demultiplexer_1_out5,
       demultiplexer_1_out7, demultiplexer_1_out8, demultiplexer_1_out10, demultiplexer_1_out11,
       demultiplexer_1_out12, demultiplexer_1_out18, demultiplexer_1_out27, demultiplexer_2_out0,
       demultiplexer_2_out2, demultiplexer_2_out3, demultiplexer_2_out4, demultiplexer_2_out5,
       demultiplexer_2_out6, demultiplexer_2_out8, demultiplexer_2_out9, demultiplexer_2_out10,
       demultiplexer_2_out11, demultiplexer_2_out12, demultiplexer_2_out13, ext_5or16, J, JAL, LW, MFLO, NOR,
       nor_1_out, not_1_out, not_2_out, OR, or_13_out, ORI, SLL, SLT, SLTI, SLTU, SRA, SRL, SUB;
  wire [0:0] \写入寄存器选择 ;
  wire [4:0] multiplexer_2_out;
  wire [31:0] bit_extender_1_out, bit_extender_3_out, bit_extender_4_out;
  wire [31:28] shifter_1_out;

  LED led_1 (.in(J));
  LED led_2 (.in(JAL));
  LED led_3 (.in(BEQ));
  LED led_4 (.in(BNE));
  LED led_5 (.in(BLEZ));
  LED led_6 (.in(ADDI));
  LED led_7 (.in(ADDIU));
  LED led_8 (.in(SLTI));
  LED led_9 (.in(ANDI));
  LED led_10 (.in(ORI));
  LED led_11 (.in(Byte));
  LED led_12 (.in(LW));
  LED led_13 (.in(\DM写入使能 ));
  // Probe on \寄存器写入数据选择2位_alu_DM_PC_LO 
  // Probe on \ALU_SRC_2位_s_ext_RFD2_s_extun_0 
  // Probe on ALU_OP
  // Probe on CMD[31:26]
  // Probe on CMD[31:26]
  // Probe on CMD[5:0]
  // Probe on CMD[5:0]
  LED led_14 (.in(SLL));
  LED led_15 (.in(SRL));
  LED led_16 (.in(SRA));
  LED led_17 (.in(JR));
  LED led_18 (.in(Systemcall));
  LED led_19 (.in(MFLO));
  LED led_20 (.in(\HILO写入使能 ));
  LED led_21 (.in(ADD));
  LED led_22 (.in(ADDU));
  LED led_23 (.in(SUB));
  LED led_24 (.in(AND));
  LED led_25 (.in(OR));
  LED led_26 (.in(NOR));
  LED led_27 (.in(SLT));
  LED led_28 (.in(SLTU));
  Demultiplexer #(.select(5), .disabled(0)) demultiplexer_1 (
    .out0(demultiplexer_1_out0), .out1(demultiplexer_1_out1), .out2(demultiplexer_1_out2),
    .out3(demultiplexer_1_out3), .out4(demultiplexer_1_out4), .out5(demultiplexer_1_out5),
    .out7(demultiplexer_1_out7), .out8(demultiplexer_1_out8), .out10(demultiplexer_1_out10),
    .out11(demultiplexer_1_out11), .out12(demultiplexer_1_out12), .out18(demultiplexer_1_out18),
    .out27(demultiplexer_1_out27), .in(1'b1), .sel(CMD[4:0]));  // open: out6, out9, out13, out14, out15, out16, out17, out19, out20, out21, out22, out23, out24, out25, out26, out28, out29, out30, out31, en
  nor nor_1 (nor_1_out, CMD[26], CMD[27], CMD[28], CMD[30], CMD[31], CMD[29]);
  not not_1 (not_1_out, CMD[5]);
  assign bit_extender_1_out = {{16{CMD[15]}}, CMD[15:0]};  // Bit_Extender bit_extender_1
  assign \unsigned  = {{16{1'b0}}, CMD[15:0]};  // Bit_Extender bit_extender_2
  assign bit_extender_3_out = {{27{1'b0}}, CMD[10:6]};  // Bit_Extender bit_extender_3
  assign bit_extender_4_out = {{6{CMD[25]}}, CMD[25:0]};  // Bit_Extender bit_extender_4
  Shifter #(.width(32)) shifter_1 (.in(bit_extender_4_out), .\dist (5'b00010), .out({shifter_1_out, imme}));
  Multiplexer #(.width(32)) multiplexer_1 (
    .in0(bit_extender_1_out), .in1(bit_extender_3_out), .out(\signed ), .sel(ext_5or16));  // open: en
  Demultiplexer #(.select(5), .disabled(0)) demultiplexer_2 (
    .out0(demultiplexer_2_out0), .out2(demultiplexer_2_out2), .out3(demultiplexer_2_out3),
    .out4(demultiplexer_2_out4), .out5(demultiplexer_2_out5), .out6(demultiplexer_2_out6),
    .out8(demultiplexer_2_out8), .out9(demultiplexer_2_out9), .out10(demultiplexer_2_out10),
    .out11(demultiplexer_2_out11), .out12(demultiplexer_2_out12), .out13(demultiplexer_2_out13), .in(1'b1),
    .sel(CMD[30:26]));  // open: out1, out7, out14, out15, out16, out17, out18, out19, out20, out21, out22, out23, out24, out25, out26, out27, out28, out29, out30, out31, en
  and _0 (SLL, demultiplexer_1_out0, nor_1_out, not_1_out);
  and _2 (SRL, demultiplexer_1_out2, nor_1_out, not_1_out);
  and _3 (SRA, demultiplexer_1_out3, nor_1_out, not_1_out);
  and _8 (JR, demultiplexer_1_out8, nor_1_out, not_1_out);
  and _12 (Systemcall, demultiplexer_1_out12, nor_1_out, not_1_out);
  and _18 (MFLO, demultiplexer_1_out18, nor_1_out, not_1_out);
  and _27 (\HILO写入使能 , demultiplexer_1_out27, nor_1_out, not_1_out);
  not not_2 (not_2_out, CMD[31]);
  and _32 (ADD, demultiplexer_1_out0, nor_1_out, CMD[5]);
  and _33 (ADDU, demultiplexer_1_out1, nor_1_out, CMD[5]);
  and _34 (SUB, demultiplexer_1_out2, nor_1_out, CMD[5]);
  and _36 (AND, demultiplexer_1_out4, nor_1_out, CMD[5]);
  and _37 (OR, demultiplexer_1_out5, nor_1_out, CMD[5]);
  and _39 (NOR, demultiplexer_1_out7, nor_1_out, CMD[5]);
  and _42 (SLT, demultiplexer_1_out10, nor_1_out, CMD[5]);
  and _43 (SLTU, demultiplexer_1_out11, nor_1_out, CMD[5]);
  LED SPECAIL (.in(nor_1_out));
  and _2_2 (J, demultiplexer_2_out2, not_2_out);
  and _3_2 (JAL, demultiplexer_2_out3, not_2_out);
  and _4 (BEQ, demultiplexer_2_out4, not_2_out);
  buf _5 (BNE, demultiplexer_2_out5);  // AND_Gate
  and _6 (BLEZ, demultiplexer_2_out6, not_2_out);
  and _8_2 (ADDI, demultiplexer_2_out8, not_2_out);
  and _9 (ADDIU, demultiplexer_2_out9, not_2_out);
  and _10 (SLTI, demultiplexer_2_out10, not_2_out);
  and _12_2 (ANDI, demultiplexer_2_out12, not_2_out);
  and _13 (ORI, demultiplexer_2_out13, not_2_out);
  and _32_2 (Byte, demultiplexer_2_out0, CMD[31]);
  and _35 (LW, demultiplexer_2_out3, CMD[31]);
  and _43_2 (\DM写入使能 , demultiplexer_2_out11, CMD[31]);
  Multiplexer #(.width(5)) multiplexer_2 (
    .in0(CMD[25:21]), .in1(CMD[20:16]), .out(multiplexer_2_out), .sel(ext_5or16));  // open: en
  Multiplexer #(.select(2), .width(5)) multiplexer_3 (
    .in0(CMD[20:16]), .in1(CMD[15:11]), .in2({5{1'b1}}), .out(RW), .sel({JAL, \写入寄存器选择 [0]}));  // open: in3, en
  Multiplexer #(.width(5)) multiplexer_4 (
    .in0(multiplexer_2_out), .in1(5'b00010), .out(RA), .sel(Systemcall));  // open: en
  or or_1 (\寄存器写入数据选择2位_alu_DM_PC_LO [1], JAL, MFLO);
  or or_2 (\寄存器写入数据选择2位_alu_DM_PC_LO [0], LW, MFLO, Byte);
  or or_3 (OP_compare[0], BNE, BLEZ);
  or or_4 (OP_compare[1], SLTI, SLTI, SLTU, BLEZ);
  or or_5 (JUMP, JR, J, JAL);
  or or_6 (Branch, BEQ, BNE, BLEZ);
  or or_7 (ext_5or16, SRL, SRA, SLL);
  or or_8 (set, SLT, SLTI, SLTU);
  or or_9 (\写入寄存器选择 [0], ADD, ADDU, AND, SLL, SRA, SRL, SUB, OR, NOR, SLT, SLTU, MFLO);
  or or_10 (\寄存器写入使能 , ADD, ADDI, ADDIU, ADDU, AND, ANDI, SLL, SRL, SRA, SUB, ORI, NOR, LW, JAL, Byte, MFLO, SLT, OR, SLTI, SLTU);
  or or_11 (\ALU_SRC_2位_s_ext_RFD2_s_extun_0 [0], ADD, ADDU, SUB, OR, NOR, SLT, BEQ, BNE, \HILO写入使能 , BLEZ, SLTU, AND);
  or or_12 (\ALU_SRC_2位_s_ext_RFD2_s_extun_0 [1], ANDI, ADDIU, BLEZ, ORI);
  or or_13 (or_13_out, BEQ, BNE, SLT, SLTI);
  or _0_2 (ALU_OP[0], or_13_out, AND, ANDI, ADD, ADDI, ADDIU, ADDU, \DM写入使能 , LW, SRA, Byte, BLEZ);
  or _2_3 (ALU_OP[1], SRL, BLEZ, SUB, NOR, or_13_out, AND, ANDI);
  or _2_4 (ALU_OP[2], \HILO写入使能 , Byte, LW, \DM写入使能 , SLTU, SUB, AND, ANDI, ADD, ADDI, ADDIU, ADDU);
  or _3_3 (ALU_OP[3], BLEZ, SLTU, or_13_out, NOR, ORI, OR);

  assign RB = CMD[20:16];

  // Other names for the same wires on the sheet: _28位立即数[27:0] = imme;
  //   ALU_SRC[1:0] = \ALU_SRC_2位_s_ext_RFD2_s_extun_0 ; FUNC[5:0] = CMD[5:0]; RD[4:0] = CMD[15:11];
  //   RT[4:0] = CMD[20:16]; RS[4:0] = CMD[25:21]; OP[5:0] = CMD[31:26]; EN_Register_write = \寄存器写入使能 ;
  //   Jump_register = JR; LB = Byte; DIVU = \HILO写入使能 ; LO_EN = \HILO写入使能 ; OP_cmp[1:0] = OP_compare;
  //   EN_DM = \DM写入使能 ; SW = \DM写入使能 ; 写入寄存器选择[1] = JAL; 寄存器写入数据选择2位[1:0] = \寄存器写入数据选择2位_alu_DM_PC_LO ;
  //   无符号拓展数[31:0] = \unsigned ; 有符号拓展数[31:0] = \signed 

  // Notes on the sheet:
  //   输入引脚区
  //   指令观察区
  //   输出引脚区
endmodule

module NPC (
  input  [31:0] _5or16,
  input  [27:0] imme,
  input  [31:0] PC,
  input  BRANCH,
  input  [31:0] RFD1,
  input  JUMP,
  input  JR,
  input  compare_result,
  output [31:0] PC_out,
  output branch_success,
  output [31:0] PC_4
);

  wire [31:0] adder_2_out, multiplexer_1_out, multiplexer_2_out, shifter_1_out;

  Adder #(.width(32)) adder_1 (.a(32'h4), .b(PC), .out(PC_4));  // open: cin, cout
  // Probe on imme
  Shifter #(.width(32)) shifter_1 (.in(_5or16), .\dist (5'b00010), .out(shifter_1_out));
  Multiplexer #(.width(32), .disabled(0)) multiplexer_1 (
    .in0({PC_4[31:28], imme}), .in1(RFD1), .out(multiplexer_1_out), .sel(JR));  // open: en
  Adder #(.width(32)) adder_2 (.a(PC_4), .b(shifter_1_out), .out(adder_2_out));  // open: cin, cout
  Multiplexer #(.width(32), .disabled(0)) multiplexer_2 (
    .in0(PC_4), .in1(adder_2_out), .out(multiplexer_2_out), .sel(branch_success));  // open: en
  and and_1 (branch_success, BRANCH, compare_result);
  Multiplexer #(.width(32), .disabled(0)) multiplexer_3 (
    .in0(multiplexer_2_out), .in1(multiplexer_1_out), .out(PC_out), .sel(JUMP));  // open: en

  // Other names for the same wires on the sheet: branch_succeed = branch_success
endmodule

// CP
module compare (
  input  [1:0] choice,
  input  \等于 ,
  input  \小于 ,
  output result
);

  wire not_1_out, or_out;

  Multiplexer #(.select(2), .disabled(0)) multiplexer_1 (
    .in0(\等于 ), .in1(not_1_out), .in2(\小于 ), .in3(or_out), .out(result), .sel(choice));  // open: en
  not not_1 (not_1_out, \等于 );
  or \or  (or_out, \等于 , \小于 );

  // Other names for the same wires on the sheet: tunnel = \小于 ; tunnel_t = \等于 
endmodule

// RE
module data_in_re (
  input  [31:0] result,
  input  [31:0] data,
  input  [1:0] sel,
  input  [31:0] PC_4,
  input  \byte ,
  input  [31:0] LO,
  input  [1:0] re_choose,
  input  in_8,
  input  set,
  output [31:0] data_in_re
);

  wire and_1_out;
  wire [7:0] multiplexer_2_out;
  wire [31:0] bit_extender_1_out, multiplexer_1_out, multiplexer_3_out;

  Multiplexer #(.width(32)) multiplexer_1 (
    .in0(data), .in1(bit_extender_1_out), .out(multiplexer_1_out), .sel(\byte ));  // open: en
  and and_1 (and_1_out, in_8, set);
  Multiplexer #(.select(2), .width(8)) multiplexer_2 (
    .in0(data[7:0]), .in1(data[15:8]), .in2(data[23:16]), .in3(data[31:24]), .out(multiplexer_2_out),
    .sel(sel));  // open: en
  Multiplexer #(.select(2), .width(32), .disabled(0)) multiplexer_3 (
    .in0(result), .in1(multiplexer_1_out), .in2(PC_4), .in3(LO), .out(multiplexer_3_out), .sel(re_choose));  // open: en
  Multiplexer #(.width(32), .disabled(0)) multiplexer_4 (
    .in0(multiplexer_3_out), .in1(32'h1), .out(data_in_re), .sel(and_1_out));  // open: en
  assign bit_extender_1_out = {{24{multiplexer_2_out[7]}}, multiplexer_2_out};  // Bit_Extender bit_extender_1
endmodule

module \分支计数  (
  input  J,
  input  B,
  input  S,
  input  T,
  output [15:0] JO,
  output [15:0] BO,
  output [15:0] BS
);

  Counter #(.width(16), .max('hffff)) counter_1 (.count(J), .Q(JO), .clk(T));  // open: load, D, carry, clr
  Counter #(.width(16), .max('hffff)) counter_2 (.count(B), .Q(BO), .clk(T));  // open: load, D, carry, clr
  Counter #(.width(16), .max('hffff)) counter_3 (.count(S), .Q(BS), .clk(T));  // open: load, D, carry, clr
endmodule
